// Logisim project comparq.circ as structural Verilog: 18 circuits, main circuit simulation
module full_adder (
  input  A,
  input  B,
  input  Ci,
  output S,
  output Co
);

  wire and_1_out, and_2_out, xor_1_out;

  xor xor_1 (xor_1_out, A, B);
  and and_1 (and_1_out, A, B);
  xor xor_2 (S, xor_1_out, Ci);
  and and_2 (and_2_out, xor_1_out, Ci);
  or or_1 (Co, and_2_out, and_1_out);

  // Notes on the sheet:
  //   Full Adder
endmodule

module _8_bit_adder (
  input  [7:0] Q1,
  input  [7:0] Q0,
  output [7:0] S
);

  wire full_adder_1_co, full_adder_2_co, full_adder_3_co, full_adder_4_co, full_adder_5_co, full_adder_6_co,
       full_adder_7_co, full_adder_8_co;
  wire [7:0] full_adder_1_s, n2x8extender_1_output;

  full_adder full_adder_1 (.A(Q1[0]), .B(Q0[0]), .Ci(1'b0), .S(full_adder_1_s[0]), .Co(full_adder_1_co));
  full_adder full_adder_2 (.A(Q1[1]), .B(Q0[1]), .Ci(full_adder_1_co), .S(full_adder_1_s[1]), .Co(full_adder_2_co));
  full_adder full_adder_3 (.A(Q1[2]), .B(Q0[2]), .Ci(full_adder_2_co), .S(full_adder_1_s[2]), .Co(full_adder_3_co));
  full_adder full_adder_4 (.A(Q1[3]), .B(Q0[3]), .Ci(full_adder_3_co), .S(full_adder_1_s[3]), .Co(full_adder_4_co));
  full_adder full_adder_5 (.A(Q1[4]), .B(Q0[4]), .Ci(full_adder_4_co), .S(full_adder_1_s[4]), .Co(full_adder_5_co));
  full_adder full_adder_6 (.A(Q1[5]), .B(Q0[5]), .Ci(full_adder_5_co), .S(full_adder_1_s[5]), .Co(full_adder_6_co));
  full_adder full_adder_7 (.A(Q1[6]), .B(Q0[6]), .Ci(full_adder_6_co), .S(full_adder_1_s[6]), .Co(full_adder_7_co));
  full_adder full_adder_8 (.A(Q1[7]), .B(Q0[7]), .Ci(full_adder_7_co), .S(full_adder_1_s[7]), .Co(full_adder_8_co));
  _2X8extender u_2x8extender_1 (.Input(full_adder_8_co), .Output(n2x8extender_1_output));
  assign S = full_adder_1_s | n2x8extender_1_output;  // OR_Gate or_1, 8 bits wide

  // Notes on the sheet:
  //   If overflow occurs
  //   sets the result to
  //   the highest possible value
endmodule

module D_flip_flop (
  input  D,
  input  C,
  output Q,
  output nQ
);

  wire nand_1_out, nand_2_out, not_1_out;

  not not_1 (not_1_out, D);
  nand nand_1 (nand_1_out, D, C);
  nand nand_2 (nand_2_out, C, not_1_out);
  nand nand_3 (Q, nand_1_out, nQ);
  nand nand_4 (nQ, Q, nand_2_out);

  // Notes on the sheet:
  //   D flip flop
endmodule

module Down_Counter (
  input  I0,
  input  I1,
  input  I2,
  input  I3,
  input  I4,
  input  I5,
  input  I6,
  input  I7,
  input  Clock,
  input  Clear,
  output out
);

  wire and_1_out, and_2_out, and_3_out, and_4_out, and_5_out, and_6_out, Q0, Q1, Q2, Q3, Q4, Q5, Q6, Q7,
       t_ff_1_qn, t_ff_2_qn, t_ff_3_qn, t_ff_4_qn, t_ff_5_qn, t_ff_6_qn, t_ff_7_qn;

  T_Flip_Flop t_ff_1 (.clk(Clock), .T(1'b1), .Q(Q0), .Qn(t_ff_1_qn), .preset(I0), .reset(Clear));  // open: en
  T_Flip_Flop t_ff_2 (.clk(Clock), .T(t_ff_1_qn), .Q(Q1), .Qn(t_ff_2_qn), .preset(I1), .reset(Clear));  // open: en
  and and_1 (and_1_out, t_ff_2_qn, t_ff_1_qn);
  nor nor_1 (out, Q0, Q1, Q2, Q3, Q4, Q5, Q6, Q7);
  T_Flip_Flop t_ff_3 (.clk(Clock), .T(and_1_out), .Q(Q2), .Qn(t_ff_3_qn), .preset(I2), .reset(Clear));  // open: en
  and and_2 (and_2_out, t_ff_3_qn, t_ff_2_qn, t_ff_1_qn);
  T_Flip_Flop t_ff_4 (.clk(Clock), .T(and_2_out), .Q(Q3), .Qn(t_ff_4_qn), .preset(I3), .reset(Clear));  // open: en
  and and_3 (and_3_out, t_ff_4_qn, t_ff_3_qn, t_ff_2_qn, t_ff_1_qn);
  T_Flip_Flop t_ff_5 (.clk(Clock), .T(and_3_out), .Q(Q4), .Qn(t_ff_5_qn), .preset(I4), .reset(Clear));  // open: en
  and and_4 (and_4_out, t_ff_5_qn, t_ff_4_qn, t_ff_3_qn, t_ff_2_qn, t_ff_1_qn);
  T_Flip_Flop t_ff_6 (.clk(Clock), .T(and_4_out), .Q(Q5), .Qn(t_ff_6_qn), .preset(I5), .reset(Clear));  // open: en
  and and_5 (and_5_out, t_ff_6_qn, t_ff_5_qn, t_ff_4_qn, t_ff_3_qn, t_ff_2_qn, t_ff_1_qn);
  T_Flip_Flop t_ff_7 (.clk(Clock), .T(and_5_out), .Q(Q6), .Qn(t_ff_7_qn), .preset(I6), .reset(Clear));  // open: en
  and and_6 (and_6_out, t_ff_7_qn, t_ff_6_qn, t_ff_5_qn, t_ff_4_qn, t_ff_3_qn, t_ff_2_qn, t_ff_1_qn);
  T_Flip_Flop t_ff_8 (.clk(Clock), .T(and_6_out), .Q(Q7), .preset(I7), .reset(Clear));  // open: Qn, en
endmodule

module multiply (
  input  [7:0] Q0,
  input  Clear,
  input  [7:0] Q1,
  input  Clock,
  output [7:0] out_5
);

  wire and_1_out, check, Counter_out, nor_1_out, not_1_out, not_3_out;
  wire [7:0] _1_to_8_bit_extender_output, Adder_s, Multiplexer_out_4, n2x8extender_1_output, register_1_r0;

  and and_1 (and_1_out, Clock, check);
  Down_Counter Counter (
    .Clock(and_1_out), .Clear(Clear), .I0(Q0[0]), .I1(Q0[1]), .I2(Q0[2]), .I3(Q0[3]), .I4(Q0[4]), .I5(Q0[5]),
    .I6(Q0[6]), .I7(Q0[7]), .out(Counter_out));
  not not_1 (not_1_out, nor_1_out);
  _2X8extender _1_to_8_bit_extender (.Input(not_1_out), .Output(_1_to_8_bit_extender_output));
  _2Multiplexer Multiplexer (
    .I0(Q1), .Selecter(_1_to_8_bit_extender_output), .out_4(Multiplexer_out_4), .I1(register_1_r0));
  _8_bit_adder Adder (.Q0(Multiplexer_out_4), .Q1(Q1), .S(Adder_s));
  nor nor_1 (nor_1_out, check, register_1_r0[0], register_1_r0[1], register_1_r0[2], register_1_r0[3], register_1_r0[4], register_1_r0[5], register_1_r0[6], register_1_r0[7]);
  Register register_1 (
    .Clock(and_1_out), .Clear(Clear), .Q0(Adder_s[0]), .Q1(Adder_s[1]), .Q2(Adder_s[2]), .Q3(Adder_s[3]),
    .Q4(Adder_s[4]), .Q5(Adder_s[5]), .Q6(Adder_s[6]), .Q7(Adder_s[7]), .R0(register_1_r0[0]),
    .R1(register_1_r0[1]), .R2(register_1_r0[2]), .R3(register_1_r0[3]), .R4(register_1_r0[4]),
    .R5(register_1_r0[5]), .R6(register_1_r0[6]), .R7(register_1_r0[7]));
  not not_2 (check, Counter_out);
  not not_3 (not_3_out, check);
  _2X8extender u_2x8extender_1 (.Input(not_3_out), .Output(n2x8extender_1_output));
  assign out_5 = register_1_r0 & n2x8extender_1_output;  // AND_Gate and_2, 8 bits wide

  // Notes on the sheet:
  //   The or gate makes sure not to multiply with zero
  //   In other words makes sure multiplication by zero is zero
endmodule

module Register (
  input  Q0,
  input  Q1,
  input  Q2,
  input  Q3,
  input  Q4,
  input  Q5,
  input  Q6,
  input  Q7,
  input  Clock,
  input  Clear,
  output R0,
  output R1,
  output R2,
  output R3,
  output R4,
  output R5,
  output R6,
  output R7
);

  D_Flip_Flop d_ff_1 (.clk(Clock), .D(Q0), .Q(R0), .reset(Clear));  // open: Qn, preset, en
  D_Flip_Flop d_ff_2 (.clk(Clock), .D(Q1), .Q(R1), .reset(Clear));  // open: Qn, preset, en
  D_Flip_Flop d_ff_3 (.clk(Clock), .D(Q2), .Q(R2), .reset(Clear));  // open: Qn, preset, en
  D_Flip_Flop d_ff_4 (.clk(Clock), .D(Q3), .Q(R3), .reset(Clear));  // open: Qn, preset, en
  D_Flip_Flop d_ff_5 (.clk(Clock), .D(Q4), .Q(R4), .reset(Clear));  // open: Qn, preset, en
  D_Flip_Flop d_ff_6 (.clk(Clock), .D(Q5), .Q(R5), .reset(Clear));  // open: Qn, preset, en
  D_Flip_Flop d_ff_7 (.clk(Clock), .D(Q6), .Q(R6), .reset(Clear));  // open: Qn, preset, en
  D_Flip_Flop d_ff_8 (.clk(Clock), .D(Q7), .Q(R7), .reset(Clear));  // open: Qn, preset, en
endmodule

module _2Multiplexer (
  input  [7:0] I0,
  input  [7:0] Selecter,
  input  [7:0] I1,
  output [7:0] out_4
);

  wire [7:0] and_1_out, and_2_out, not_1_out;

  assign not_1_out = ~Selecter;  // NOT_Gate not_1, 8 bits wide
  assign and_1_out = I0 & not_1_out;  // AND_Gate and_1, 8 bits wide
  assign and_2_out = Selecter & I1;  // AND_Gate and_2, 8 bits wide
  assign out_4 = and_1_out | and_2_out;  // OR_Gate or_1, 8 bits wide
endmodule

module J_K_flip_flop (
  input  J,
  input  C,
  input  K,
  output Q,
  output nQ
);

  wire nand_1_out, nand_2_out;

  nand nand_1 (nand_1_out, J, nQ, C);
  nand nand_2 (nand_2_out, C, Q, K);
  nand nand_3 (Q, nand_1_out, nQ);
  nand nand_4 (nQ, Q, nand_2_out);

  // Notes on the sheet:
  //   J K flip flop
endmodule

module ALU (
  input  [2:0] OPcode,
  input  Clear,
  input  [7:0] A,
  input  [7:0] B,
  output [7:0] Output
);

  wire Clock;
  wire [7:0] add, addB, And, AndB, Default, DefaultB, Div, DivB, mul, mulB, n2x8extender_1_output, Not, NotB,
       oadd, oAnd, oDiv, omul, oNot, oOr, Or, OrB, osub, sub, subB;

  Deplexer deplexer_1 (
    .Data(A), .S2(OPcode[2]), .S1(OPcode[1]), .S0(OPcode[0]), ._111(add), ._110(sub), ._101(mul), ._100(Div),
    ._011(And), ._010(Or), ._001(Not), ._000(Default));
  Deplexer deplexer_2 (
    .Data(B), .S2(OPcode[2]), .S1(OPcode[1]), .S0(OPcode[0]), ._111(addB), ._110(subB), ._101(mulB),
    ._100(DivB), ._011(AndB), ._010(OrB), ._001(NotB), ._000(DefaultB));
  Clock u_Clock (.out(Clock));
  multiply Multiplier (.Q0(mul), .Clear(Clock), .Q1(mulB), .Clock(Clear), .out_5(omul));
  _8_bit_adder Adder (.Q0(add), .Q1(addB), .S(oadd));
  assign oAnd = And & AndB;  // AND_Gate and_1, 8 bits wide
  assign oNot = Not ^ NotB;  // XOR_Gate xor_1, 8 bits wide
  _2X8extender u_2x8extender_1 (.Input(1'b0), .Output(n2x8extender_1_output));
  subtractor Subtractor (.A(sub), .B(subB), .OUT(osub));
  dividor Dividor (.A(Div), .B(DivB), .OUT(oDiv));
  assign oOr = Or | OrB;  // OR_Gate or_1, 8 bits wide
  multiplexer multiplexer_1 (
    ._111(oadd), ._110(osub), ._101(omul), ._100(oDiv), ._011(oAnd), ._010(oOr), ._001(oNot),
    ._000(n2x8extender_1_output), .S2(OPcode[2]), .S1(OPcode[1]), .S0(OPcode[0]), .Data(Output));

  // Notes on the sheet:
  //   111
  //   101
  //   011
  //   001
  //   110
  //   100
  //   010
endmodule

module _2X8extender (
  input  Input,
  output [7:0] Output
);


  assign Output = {8{Input}};

  // Other names for the same wires on the sheet: I = Input
endmodule

module _2_s_complement (
  input  [7:0] in,
  output [7:0] out
);

  wire [0:0] not_1_out;
  wire [7:0] not_2_out;

  not not_1 (not_1_out[0], 1'b0);
  assign not_2_out = ~in;  // NOT_Gate not_2, 8 bits wide
  _8_bit_adder u_8_bit_adder_1 (.Q0(not_2_out), .Q1({{7{1'b0}}, not_1_out[0]}), .S(out));
endmodule

module subtractor (
  input  [7:0] A,
  input  [7:0] B,
  output [7:0] OUT
);

  wire [7:0] n2_s_complement_1_out;

  _2_s_complement u_2_s_complement_1 (.in(B), .out(n2_s_complement_1_out));
  _8_bit_adder u_8_bit_adder_1 (.Q0(A), .Q1(n2_s_complement_1_out), .S(OUT));
endmodule

module counter (
  input  counter,
  input  clear,
  output [7:0] out_3
);

  up_counter up_counter_1 (
    .Clock(counter), .Clear(clear), .I0(1'b0), .I1(1'b0), .I2(1'b0), .I3(1'b0), .I4(1'b0), .I5(1'b0),
    .I6(1'b0), .I7(1'b0), .out(out_3));
endmodule

module up_counter (
  input  I0,
  input  I1,
  input  I2,
  input  I3,
  input  I4,
  input  I5,
  input  I6,
  input  I7,
  input  Clock,
  input  Clear,
  output [7:0] out
);

  wire and_1_out, and_2_out, and_3_out, and_4_out, and_5_out, and_6_out;

  T_Flip_Flop t_ff_1 (.clk(Clock), .T(1'b1), .Q(out[0]), .preset(I0), .reset(Clear));  // open: Qn, en
  T_Flip_Flop t_ff_2 (.clk(Clock), .T(out[0]), .Q(out[1]), .preset(I1), .reset(Clear));  // open: Qn, en
  and and_1 (and_1_out, out[0], out[1]);
  T_Flip_Flop t_ff_3 (.clk(Clock), .T(and_1_out), .Q(out[2]), .preset(I2), .reset(Clear));  // open: Qn, en
  and and_2 (and_2_out, out[0], out[1], out[2]);
  T_Flip_Flop t_ff_4 (.clk(Clock), .T(and_2_out), .Q(out[3]), .preset(I3), .reset(Clear));  // open: Qn, en
  and and_3 (and_3_out, out[0], out[1], out[2], out[3]);
  T_Flip_Flop t_ff_5 (.clk(Clock), .T(and_3_out), .Q(out[4]), .preset(I4), .reset(Clear));  // open: Qn, en
  and and_4 (and_4_out, out[0], out[1], out[2], out[3], out[4]);
  T_Flip_Flop t_ff_6 (.clk(Clock), .T(and_4_out), .Q(out[5]), .preset(I5), .reset(Clear));  // open: Qn, en
  and and_5 (and_5_out, out[0], out[1], out[2], out[3], out[4], out[5]);
  T_Flip_Flop t_ff_7 (.clk(Clock), .T(and_5_out), .Q(out[6]), .preset(I6), .reset(Clear));  // open: Qn, en
  and and_6 (and_6_out, out[0], out[1], out[2], out[3], out[4], out[5], out[6]);
  T_Flip_Flop t_ff_8 (.clk(Clock), .T(and_6_out), .Q(out[7]), .preset(I7), .reset(Clear));  // open: Qn, en

  // Other names for the same wires on the sheet: Q0 = out[0]; Q1 = out[1]; Q2 = out[2]; Q3 = out[3]; Q4 = out[4];
  //   Q5 = out[5]; Q6 = out[6]; Q7 = out[7]
endmodule

module dividor (
  input  [7:0] A,
  input  [7:0] B,
  output [7:0] OUT
);

  wire n2_s_complement_2_p1, undriven;
  wire [7:0] n2_s_complement_1_out, n2multiplexer_1_out_4, n2x8extender_1_output, n8_bit_adder_1_s,
       register_1_r0;

  _2_s_complement u_2_s_complement_1 (.in(B), .out(n2_s_complement_1_out));
  _2Multiplexer u_2multiplexer_1 (
    .I0(register_1_r0), .Selecter(n2x8extender_1_output), .out_4(n2multiplexer_1_out_4),
    .I1(n2_s_complement_1_out));
  _8_bit_adder u_8_bit_adder_1 (.Q0(A), .Q1(n2multiplexer_1_out_4), .S(n8_bit_adder_1_s));
  _2X8extender u_2x8extender_1 (.Input(n2_s_complement_2_p1), .Output(n2x8extender_1_output));
  Register register_1 (
    .Clear(undriven), .Q0(n8_bit_adder_1_s[0]), .Q1(n8_bit_adder_1_s[1]), .Q2(n8_bit_adder_1_s[2]),
    .Q3(n8_bit_adder_1_s[3]), .Q4(n8_bit_adder_1_s[4]), .Q5(n8_bit_adder_1_s[5]), .Q6(n8_bit_adder_1_s[6]),
    .Q7(n8_bit_adder_1_s[7]), .R0(register_1_r0[0]), .R1(register_1_r0[1]), .R2(register_1_r0[2]),
    .R3(register_1_r0[3]), .R4(register_1_r0[4]), .R5(register_1_r0[5]), .R6(register_1_r0[6]),
    .R7(register_1_r0[7]));  // open: Clock
  // _2_s_complement 2_s_complement_2: pin names not known; wires that end beside it: n2_s_complement_2_p1, register_1_r0
  counter counter_1 (.counter(register_1_r0[7]), .clear(register_1_r0[7]), .out_3(OUT));
endmodule

module Deplexer (
  input  S2,
  input  S1,
  input  S0,
  input  [7:0] Data,
  output [7:0] _111,
  output [7:0] _110,
  output [7:0] _101,
  output [7:0] _100,
  output [7:0] _011,
  output [7:0] _010,
  output [7:0] _001,
  output [7:0] _000
);

  wire [7:0] n2x8extender_1_output, n2x8extender_2_output, n2x8extender_3_output, not_1_out, not_2_out,
       not_3_out;

  _2X8extender u_2x8extender_1 (.Input(S2), .Output(n2x8extender_1_output));
  assign not_1_out = ~n2x8extender_1_output;  // NOT_Gate not_1, 8 bits wide
  _2X8extender u_2x8extender_2 (.Input(S1), .Output(n2x8extender_2_output));
  assign not_2_out = ~n2x8extender_2_output;  // NOT_Gate not_2, 8 bits wide
  _2X8extender u_2x8extender_3 (.Input(S0), .Output(n2x8extender_3_output));
  assign not_3_out = ~n2x8extender_3_output;  // NOT_Gate not_3, 8 bits wide
  assign _111 = n2x8extender_1_output & n2x8extender_2_output & n2x8extender_3_output & Data;  // AND_Gate and_1, 8 bits wide
  assign _110 = n2x8extender_1_output & n2x8extender_2_output & not_3_out & Data;  // AND_Gate and_2, 8 bits wide
  assign _101 = n2x8extender_1_output & not_2_out & n2x8extender_3_output & Data;  // AND_Gate and_3, 8 bits wide
  assign _100 = n2x8extender_1_output & not_2_out & not_3_out & Data;  // AND_Gate and_4, 8 bits wide
  assign _011 = not_1_out & n2x8extender_2_output & n2x8extender_3_output & Data;  // AND_Gate and_5, 8 bits wide
  assign _010 = not_1_out & n2x8extender_2_output & not_3_out & Data;  // AND_Gate and_6, 8 bits wide
  assign _001 = not_1_out & not_2_out & n2x8extender_3_output & Data;  // AND_Gate and_7, 8 bits wide
  assign _000 = not_1_out & not_2_out & not_3_out & Data;  // AND_Gate and_8, 8 bits wide
endmodule

module multiplexer (
  input  S2,
  input  S1,
  input  S0,
  input  [7:0] _111,
  input  [7:0] _110,
  input  [7:0] _101,
  input  [7:0] _100,
  input  [7:0] _011,
  input  [7:0] _010,
  input  [7:0] _001,
  input  [7:0] _000,
  output [7:0] Data
);

  wire [7:0] and_1_out, and_2_out, and_3_out, and_4_out, and_5_out, and_6_out, and_7_out, and_8_out,
       n2x8extender_1_output, n2x8extender_2_output, n2x8extender_3_output, not_1_out, not_2_out, not_3_out;

  _2X8extender u_2x8extender_1 (.Input(S2), .Output(n2x8extender_1_output));
  assign not_1_out = ~n2x8extender_1_output;  // NOT_Gate not_1, 8 bits wide
  _2X8extender u_2x8extender_2 (.Input(S1), .Output(n2x8extender_2_output));
  assign not_2_out = ~n2x8extender_2_output;  // NOT_Gate not_2, 8 bits wide
  _2X8extender u_2x8extender_3 (.Input(S0), .Output(n2x8extender_3_output));
  assign not_3_out = ~n2x8extender_3_output;  // NOT_Gate not_3, 8 bits wide
  assign and_1_out = n2x8extender_1_output & n2x8extender_2_output & n2x8extender_3_output & _111;  // AND_Gate and_1, 8 bits wide
  assign and_2_out = n2x8extender_1_output & n2x8extender_2_output & not_3_out & _110;  // AND_Gate and_2, 8 bits wide
  assign and_3_out = n2x8extender_1_output & not_2_out & n2x8extender_3_output & _101;  // AND_Gate and_3, 8 bits wide
  assign and_4_out = n2x8extender_1_output & not_2_out & not_3_out & _100;  // AND_Gate and_4, 8 bits wide
  assign and_5_out = not_1_out & n2x8extender_2_output & n2x8extender_3_output & _011;  // AND_Gate and_5, 8 bits wide
  assign and_6_out = not_1_out & n2x8extender_2_output & not_3_out & _010;  // AND_Gate and_6, 8 bits wide
  assign and_7_out = not_1_out & not_2_out & n2x8extender_3_output & _001;  // AND_Gate and_7, 8 bits wide
  assign and_8_out = not_1_out & not_2_out & not_3_out & _000;  // AND_Gate and_8, 8 bits wide
  assign Data = and_1_out | and_2_out | and_3_out | and_4_out | and_5_out | and_6_out | and_7_out | and_8_out;  // OR_Gate or_1, 8 bits wide
endmodule

module simulation (
  input  [2:0] OPcode,
  input  Clear,
  input  [7:0] A,
  input  [7:0] B,
  output [7:0] OUTPUT
);

  ALU ALU (.A(A), .B(B), .OPcode(OPcode), .Clear(Clear), .Output(OUTPUT));

  // Notes on the sheet:
  //   OPcodes
  //   111       ADD
  //   110        SUB
  //   101        MUL
  //   100         DIV
  //   011        AND
  //   010          OR
  //   001        XOR
  //   000      ZERO
endmodule
